// Logisim project archiMinimale.circ as structural Verilog: 1 circuit, main circuit main
module main (
  input  H,
  input  Raz
);

  wire branch, emem, ereg, immrt, not_1_out, not_2_out, registerfile_1_p8, rtrd, tunnel, ualmem;
  wire [3:0] op;
  wire [4:0] multiplexer_1_out, num_rd, num_rs, num_rt, rs, shamt;
  wire [5:0] co, nf;
  wire [31:0] adder_1_p2, adder_1_p3, imm32, multiplexer_2_out, res, rt;

  // Adder adder_1: pin names not known; wires that end beside it: 32'h4, adder_1_p2, adder_1_p3, adder_1_p2
  Register #(.width(32), .trigger("falling")) register_1 (
    .D(adder_1_p3), .en(1'b1), .Q(adder_1_p2), .clk(H), .clr(Raz));
  // PLA pla_1: pin names not known; wires that end beside it: co, {emem, ereg, branch, ualmem, immrt, rtrd}
  // Probe on adder_1_p2
  not not_1 (not_1_out, ereg);
  Multiplexer #(.width(5), .enable("false")) multiplexer_1 (
    .in0(num_rt), .in1(num_rd), .out(multiplexer_1_out), .sel(rtrd));
  // RegisterFile registerfile_1: pin names not known; wires that end beside it: res, H, not_1_out, multiplexer_1_out, num_rs, num_rt, Raz, registerfile_1_p8, rt
  // MIPSProgramROM mipsprogramrom_1: pin names not known; wires that end beside it: {co, num_rs, num_rt, num_rd, shamt, nf}
  // Probe on {co, num_rs, num_rt, num_rd, shamt, nf}
  Multiplexer #(.width(32), .enable("false")) multiplexer_2 (
    .in0(imm32), .in1(rt), .out(multiplexer_2_out), .sel(immrt));
  // PLA PLA_2: pin names not known; wires that end beside it: {nf, co}, op
  // MIPS_ALU mips_alu_1: pin names not known; wires that end beside it: registerfile_1_p8, multiplexer_2_out, op, tunnel, res
  // Probe on imm32
  // Probe on rs
  assign imm32 = {{16{1'b0}}, {num_rd, shamt, nf}};  // Bit_Extender bit_extender_1
  // Probe on res
  // Probe on co
  // Probe on shamt
  // Probe on nf
  // Probe on imm32
  // Probe on num_rs
  // Probe on num_rt
  // Probe on num_rd
  // Probe on rtrd
  // Probe on immrt
  // Probe on ualmem
  // Probe on branch
  // Probe on not_2_out
  not not_2 (not_2_out, ereg);
  // Probe on emem
  // Probe on op

  // Other names for the same wires on the sheet: _0 = Raz
endmodule
